# Fritzing sketch schematic (saved by Fritzing 0.8.7b)
breadboards: 1

parts:
  U1 = atmega328 [package=dip]
  IC1 = L293D [package=THT]
  ISP_HEADER = shrouded pin header, 10 pins [form="♂ (shrouded male)"]
  FRONT_SENSOR_HEADER = female pin header, 4 pins [form="♀ (female)"]
  R1 = Resistor [tolerance=±5% resistance=10k package=THT]
  C1 = Ceramic Capacitor [capacitance=100nF package="100 mil [THT, multilayer]"]
  C2 = Electrolytic Capacitor [capacitance=2.2µF package="100 mil [THT, electrolytic]"]
  C3 = Ceramic Capacitor [capacitance=100nF package="100 mil [THT, multilayer]"]
  C4 = Ceramic Capacitor [capacitance=100nF package="100 mil [THT, multilayer]"]
  L1 = Inductor [inductance=10µH package="400 mil [THT]"]
  RIGHT_MOTOR = DC Motor
  LEFT_MOTOR = DC Motor
  RIGHT_SENSOR_HEADER = female pin header, 4 pins [form="♀ (female)"]
  LEFT_SENSOR_HEADER = female pin header, 4 pins [form="♀ (female)"]
  C5 = Ceramic Capacitor [capacitance=100nF package="100 mil [THT, multilayer]"]
  C6 = Electrolytic Capacitor [capacitance=0.1mF package="100 mil [THT, electrolytic]"]
  R2 = Resistor [tolerance=±5% resistance=220 package=THT]
  RIGHT_IR_LED = LED - 5mm [color="Infrared (940nm)" package="5 mm [THT]"]
  LEFT_IR_LED = LED - 5mm [color="Infrared (940nm)" package="5 mm [THT]"]
  RIGHT_IR_PT = LTR-301 [package=ltr-301]
  LEFT_IR_PT = LTR-301 [package=ltr-301]
  BLUETOOTH_HEADER = female pin header, 6 pins [form="♀ (female)"]
  D2 = Zener Diode [breakdown_voltage=3.3V part_number=1N4732A package="Melf DO-213 AB [SMD]"]
  XTAL1 = Crystal [frequency="16 Mhz" package=THT]
  C7 = Ceramic Capacitor [capacitance=22pF package="100 mil [THT, multilayer]"]
  C8 = Ceramic Capacitor [capacitance=22pF package="100 mil [THT, multilayer]"]
  R6 = Resistor [tolerance=±5% resistance=220 package=THT]
  LED1 = LED - 5mm [color="Red (633nm)" package="5 mm [THT]"]
  S1 = Pushbutton [package=THT]
  R7 = Resistor [tolerance=±5% resistance=220 package=THT]
  C9 = Ceramic Capacitor [capacitance=100nF package="100 mil [THT, multilayer]"]
  C10 = Electrolytic Capacitor [capacitance=4.7µF package="100 mil [THT, electrolytic]"]
  R8 = Resistor [tolerance=±5% resistance=220 package=THT]
  C11 = Ceramic Capacitor [capacitance=100nF package="100 mil [THT, multilayer]"]
  C12 = Ceramic Capacitor [capacitance=100nF package="100 mil [THT, multilayer]"]

nets:
  ISP RESET: U1.RESET, ISP_HEADER.pin5, R1.Pin_1
  N1: U1.D0_(RX), BLUETOOTH_HEADER.pin4
  N2: U1.D1_(TX), R7.Pin_1
  N3: U1.D2, RIGHT_IR_PT.C
  N4: U1.D3_(PWM), LEFT_IR_PT.C
  N5: U1.D4, R6.Pin_1
  5V: U1.VCC, IC1.+V, FRONT_SENSOR_HEADER.pin1, R1.Pin_0, C1.1, C2.+, L1.pin_1, RIGHT_SENSOR_HEADER.pin1, LEFT_SENSOR_HEADER.pin1, C5.1, C6.+, R2.Pin_1, BLUETOOTH_HEADER.pin2, R8.Pin_1
  GND: U1.GND, IC1.0V, ISP_HEADER.pin10, FRONT_SENSOR_HEADER.pin4, C1.0, C2.-, C3.1, C4.1, RIGHT_SENSOR_HEADER.pin4, LEFT_SENSOR_HEADER.pin4, C5.0, C6.-, RIGHT_IR_LED.cathode, LEFT_IR_LED.cathode, RIGHT_IR_PT.E, LEFT_IR_PT.E, BLUETOOTH_HEADER.pin3, D2.anode, C7.0, C8.0, LED1.cathode, S1.leg0, C9.0, C10.-
  N6: U1.XLAT1, XTAL1.pin_0, C8.1
  N7: U1.XLAT2, XTAL1.pin_1, C7.1
  RIGHT PWM: U1.D5_(PWM), IC1.Enable_1
  LEFT PWM: U1.D6_(PWM), IC1.Enable_2
  LEFT DIR 2: U1.D7, IC1.In_4
  LEFT DIR 1: U1.D8, IC1.In_3
  RIGHT DIR 1: U1.D9_(PWM), IC1.In_1
  RIGHT DIR 2: U1.D10_(PWM), IC1.In_2
  ISP MOSI: U1.D11_(PWM), ISP_HEADER.pin1, S1.leg1
  ISP MISO: U1.D12, ISP_HEADER.pin9
  ISP SCK: U1.D13, ISP_HEADER.pin7
  N8: U1.AVCC, C4.0, L1.pin_0
  N9: U1.AREF, C3.0
  N10: U1.A0, RIGHT_SENSOR_HEADER.pin3
  N11: U1.A1, RIGHT_SENSOR_HEADER.pin2
  N12: U1.A2, LEFT_SENSOR_HEADER.pin3
  N13: U1.A3, LEFT_SENSOR_HEADER.pin2
  N14: U1.A4, FRONT_SENSOR_HEADER.pin3
  N15: U1.A5, FRONT_SENSOR_HEADER.pin2
  N16: IC1.Out_1_(_Controlled_by_Enable_1_), RIGHT_MOTOR.pin_1, C11.1
  N17: IC1.Out_2_(_Controlled_by_Enable_1_), RIGHT_MOTOR.pin_2, C11.0
  UMotors: IC1.+Vmotor, C9.1, C10.+
  N18: IC1.Out_3_(_Controlled_by_Enable_2_), LEFT_MOTOR.pin_2, C12.0
  N19: IC1.Out_4_(_Controlled_by_Enable_2_), LEFT_MOTOR.pin_1, C12.1
  N20: R2.Pin_0, RIGHT_IR_LED.anode
  N21: LEFT_IR_LED.anode, R8.Pin_0
  N22: BLUETOOTH_HEADER.pin5, D2.cathode, R7.Pin_0
  N23: R6.Pin_0, LED1.anode

notes:
  Obstacle avoiding and RC robot, Author: Szymon Katra, 1
  C11 and C12 should be across motor terminals
  Additionaly, you can solder two 100 nF capacitors
  to each motor across each terminal of motor and its case
  Pair of IR LED and IR Phototransistor can be replaced
  with optocoupler for example TCST1103
  HC-05 Bluetooth module (5V power tolerant)
  HC-SR04 Ultrasonic ranging modules
  UMotors typically 5 - 7 V
  Remember that there is voltage drop on L293D
